# Fritzing sketch Henry Chen - 22703907 PCB Design (saved by Fritzing 0.9.4)
circuit board: 8.39208cm x 4.38885cm
breadboards: 1

parts:
  U1 = 3.5mm Audio Jack [package=audio-jack]
  IC1 = PICAXE-08 [package=THT]
  C1 = Electrolytic Capacitor [capacitance=1µF package="100 mil [THT, electrolytic]"]
  C2 = Electrolytic Capacitor [capacitance=1µF package="100 mil [THT, electrolytic]"]
  C3 = Ceramic Capacitor [capacitance=100nF package="100 mil [THT, multilayer]"]
  SPKR1 = Loudspeaker
  LED1 = LED - 5mm [color="Red (633nm)" package="5 mm [THT]"]
  LED2 = LED - 5mm [color="Red (633nm)" package="5 mm [THT]"]
  LED3 = LED - 5mm [color="Red (633nm)" package="5 mm [THT]"]
  LED4 = LED - 5mm [color="Red (633nm)" package="5 mm [THT]"]
  LED5 = LED - 5mm [color="Red (633nm)" package="5 mm [THT]"]
  LED6 = LED - 5mm [color="Red (633nm)" package="5 mm [THT]"]
  LED7 = LED - 5mm [color="Red (633nm)" package="5 mm [THT]"]
  ANT1 = Antenna
  V1 = DC Power [voltage=5]
  R4 = Resistor [tolerance=±5% resistance=220 package=THT]
  R5 = Resistor [tolerance=±5% resistance=220 package=THT]
  R6 = Resistor [tolerance=±5% resistance=220 package=THT]

nets:
  GND: U1.RIGHT, IC1.0V, C1.-, SPKR1.pin2, LED1.cathode, LED2.cathode, LED3.cathode, LED4.cathode, LED5.cathode, LED6.cathode, LED7.cathode, V1.V-, R4.Pin_1
  N1: U1.SLEEVE, IC1.Serial_Out_/_Out_0, R6.Pin_0
  N2: U1.LEFT, R4.Pin_0, R5.Pin_1
  N3: IC1.+V, C1.+, V1.V+
  N4: IC1.Serial_In, R5.Pin_0
  N5: IC1.In/Out_4, LED5.anode, LED6.anode, LED7.anode, R6.Pin_1
  N6: IC1.In_3, C3.0, ANT1.antenna_lead
  N7: IC1.In/Out_2, C2.+, C3.1
  N8: IC1.In/Out_1, LED1.anode, LED2.anode, LED3.anode, LED4.anode
  N9: C2.-, SPKR1.pin1
